// Logisim project Ctl_Data_Processing.circ as structural Verilog: 1 circuit, main circuit Data_Processing
module Data_Processing (
  input  Enable,
  input  [15:0] Instruction,
  output [2:0] Rd,
  output [2:0] Rn,
  output [2:0] Rm,
  output [3:0] ALU_Opcode,
  output [3:0] Flags_Update_Mask
);

  wire and_1_out, and_2_out;
  wire [1:0] FLAG_OUT;
  wire [2:0] RM_OUT;

  Multiplexer #(.select(4)) multiplexer_1 (
    .in0(1'b0), .in1(1'b0), .in2(1'b0), .in3(1'b0), .in4(1'b0), .in5(1'b1), .in6(1'b1), .in7(1'b0),
    .in8(1'b0), .in9(1'b1), .in10(1'b1), .in11(1'b1), .in12(1'b0), .in13(1'b0), .in14(1'b0), .in15(1'b0),
    .out(FLAG_OUT[0]), .sel(Instruction[9:6]));  // open: en
  and and_1 (and_1_out, Instruction[6], ~Instruction[7], Instruction[8], Instruction[9]);  // AND_Gate
  Multiplexer #(.enable("false"), .width(3)) multiplexer_2 (
    .in0(Instruction[2:0]), .in1(Instruction[5:3]), .out(RM_OUT), .sel(and_1_out));
  and and_2 (and_2_out, and_1_out, Instruction[8]);
  not not_1 (FLAG_OUT[1], and_2_out);
  Pull_Resistor pull_resistor_1 (.node(Rd));
  assign Rd = Enable ? Instruction[2:0] : 3'bz;  // Controlled_Buffer controlled_buffer_1
  Pull_Resistor pull_resistor_2 (.node(Rn));
  assign Rn = Enable ? RM_OUT : 3'bz;  // Controlled_Buffer controlled_buffer_2
  Pull_Resistor pull_resistor_3 (.node(Rm));
  assign Rm = Enable ? RM_OUT : 3'bz;  // Controlled_Buffer controlled_buffer_3
  Pull_Resistor pull_resistor_4 (.node(ALU_Opcode));
  assign ALU_Opcode = Enable ? Instruction[9:6] : 4'bz;  // Controlled_Buffer controlled_buffer_4
  Pull_Resistor pull_resistor_5 (.node(Flags_Update_Mask));
  assign Flags_Update_Mask = Enable ? {2'b11, FLAG_OUT} : 4'bz;  // Controlled_Buffer controlled_buffer_5

  // Other names for the same wires on the sheet: INS[15:0] = Instruction; RD_OUT[2:0] = Instruction[2:0];
  //   ALU_OUT[3:0] = Instruction[9:6]; RN_OUT[2:0] = RM_OUT

  // Notes on the sheet:
  //   Note 2: RSB instruction has Rn as 1st operand.
  //   MUL instruction has Rn as 1st operand and Rdm as 2nd operand
  //   For simplification purposes, Rm is used for 1st operand both here and in the ALU.
  //   Note: instructions that does not save the result will still have the second operand as the destination register, the ALU will copy the second register to the destination register
  //   Pull output low on Enable = 0
endmodule
